# Fritzing sketch Power Manager Old (saved by Fritzing 0.9.2b)
breadboards: 1

parts:
  Raspberry_Pi1 = Raspberry Pi B rev2  # not connected
  1N4004 = Diode [package=diode-1n4001]
  1N4004_2 = Diode [package=diode-1n4001]
  1N4004_3 = Diode [package=diode-1n4001]
  Q1 = Basic FET N-Channel [package="D2Pak [SMD]"]
  Q2 = Basic FET N-Channel [package="D2Pak [SMD]"]
  Q3 = Basic FET N-Channel [package="D2Pak [SMD]"]
  Pi1 = Adafruit Pi Cobbler  # not connected
  IC1 = MCP23017 I2C I/O Expander
  Appliance_#1 = 2.1mm Barrel Jack with Terminal Block
  Q4 = Basic FET N-Channel [package="D2Pak [SMD]"]
  1N4004_4 = Diode [package=diode-1n4001]
  Appliance_#2 = 2.1mm Barrel Jack with Terminal Block
  Appliance_#3 = 2.1mm Barrel Jack with Terminal Block
  Appliance_#4 = 2.1mm Barrel Jack with Terminal Block
  12V_Power_Supply = 2.1mm Barrel Jack with Terminal Block
  J1 = screw terminal, 10 pins
  R1 = Resistor [tolerance=±5% resistance=220 package=THT]
  R2 = Resistor [tolerance=±5% resistance=220 package=THT]
  R3 = Resistor [tolerance=±5% resistance=220 package=THT]
  R4 = Resistor [tolerance=±5% resistance=220 package=THT]
  R5 = Resistor [tolerance=±5% resistance=220 package=THT]
  LED1 = LED - 5mm [color="Red (633nm)" package="5 mm [THT]"]
  LED2 = LED - 5mm [color="Red (633nm)" package="5 mm [THT]"]
  LED3 = LED - 5mm [color="Red (633nm)" package="5 mm [THT]"]
  LED4 = LED - 5mm [color="Red (633nm)" package="5 mm [THT]"]
  LED5 = LED - 5mm [color="Red (633nm)" package="5 mm [THT]"]
  S1 = Pushbutton [package="[THT]"]
  S2 = Pushbutton [package="[THT]"]
  S3 = Pushbutton [package="[THT]"]
  S4 = Pushbutton [package="[THT]"]
  S5 = Pushbutton [package="[THT]"]
  R6 = Resistor [tolerance=±5% resistance=10k package=THT]
  R7 = Resistor [tolerance=±5% resistance=10k package=THT]
  R8 = Resistor [tolerance=±5% resistance=10k package=THT]
  R9 = Resistor [tolerance=±5% resistance=10k package=THT]
  SW1 = PowerSwitch Tail II

nets:
  N1: 1N4004.A, Q2.drain, Appliance_#2.NEG, J1.pin3
  N2: 1N4004.C, 1N4004_2.C, 1N4004_3.C, Appliance_#1.POS, 1N4004_4.C, Appliance_#2.POS, Appliance_#3.POS, Appliance_#4.POS, 12V_Power_Supply.POS, J1.pin2, J1.pin4, J1.pin6, J1.pin8, J1.pin10
  N3: 1N4004_2.A, Q1.drain, Appliance_#1.NEG, J1.pin1
  N4: 1N4004_3.A, Q3.drain, Appliance_#3.NEG, J1.pin5
  N5: Q1.Gate, IC1.GPA0, R6.Pin_1
  N6: Q1.source, Q2.source, Q3.source, Q4.source, 12V_Power_Supply.NEG, J1.pin9
  N7: Q2.Gate, IC1.GPA1, R7.Pin_1
  N8: Q3.Gate, IC1.GPA2, R8.Pin_1
  N9: IC1.GPB0, S5.Pin_3, S5.Pin_4
  N10: IC1.GPB2, R1.Pin_0
  N11: IC1.GPB3, R2.Pin_0
  N12: IC1.GPB4, R3.Pin_0
  N13: IC1.GPB5, R4.Pin_0
  N14: IC1.GPB6, R5.Pin_0
  N15: IC1.VSS, LED1.cathode, LED2.cathode, LED3.cathode, LED4.cathode, LED5.cathode
  N16: IC1.A0, IC1.A1, IC1.A2, S1.Pin_2, S2.Pin_1, S2.Pin_2, S3.Pin_1, S3.Pin_2, S4.Pin_1, S4.Pin_2, S5.Pin_1, S5.Pin_2, R6.Pin_0, R7.Pin_0, R8.Pin_0, R9.Pin_0, SW1.-in
  N17: IC1.GPA3, Q4.Gate, R9.Pin_1
  N18: IC1.GPA4, S1.Pin_3, S1.Pin_4
  N19: IC1.GPA5, S2.Pin_3, S2.Pin_4
  N20: IC1.GPA6, S3.Pin_3, S3.Pin_4
  N21: IC1.GPA7, S4.Pin_3, S4.Pin_4
  N22: Q4.drain, 1N4004_4.A, Appliance_#4.NEG, J1.pin7

custom parts:
  Adafruit Pi Cobbler: Adafruit Pi Cobbler GPIO Breakout for Raspberry Pi
  MCP23017 I2C I/O Expander: The MCP23017 uses two i2c pins (these can be shared with other i2c devices), and in exchange gives you 16 general purpose pins. You can set each of 16 pins to be input, output, input with a pullup or open drain. There's even the ability to get an interrupt via an external pin when any of the inputs change so you don't have to keep polling the chip.
