# Fritzing sketch Power Manager (saved by Fritzing 0.9.2b)
breadboards: 1

parts:
  Raspberry_Pi1 = Raspberry Pi B rev2  # not connected
  Pi1 = Adafruit Pi Cobbler  # not connected
  IC1 = MCP23017 I2C I/O Expander
  Appliance_#1 = 2.1mm Barrel Jack with Terminal Block
  Appliance_#2 = 2.1mm Barrel Jack with Terminal Block
  Appliance_#3 = 2.1mm Barrel Jack with Terminal Block
  Appliance_#4 = 2.1mm Barrel Jack with Terminal Block
  12V_Power_Supply = 2.1mm Barrel Jack with Terminal Block
  R1 = Resistor [tolerance=±5% resistance=220 package=THT]
  R2 = Resistor [tolerance=±5% resistance=220 package=THT]
  R3 = Resistor [tolerance=±5% resistance=220 package=THT]
  R4 = Resistor [tolerance=±5% resistance=220 package=THT]
  R5 = Resistor [tolerance=±5% resistance=220 package=THT]
  LED1 = LED - 5mm [color="Red (633nm)" package="5 mm [THT]"]
  LED2 = LED - 5mm [color="Red (633nm)" package="5 mm [THT]"]
  LED3 = LED - 5mm [color="Red (633nm)" package="5 mm [THT]"]
  LED4 = LED - 5mm [color="Red (633nm)" package="5 mm [THT]"]
  LED5 = LED - 5mm [color="Red (633nm)" package="5 mm [THT]"]
  S1 = Pushbutton [package="[THT]"]
  S2 = Pushbutton [package="[THT]"]
  S3 = Pushbutton [package="[THT]"]
  S4 = Pushbutton [package="[THT]"]
  S5 = Pushbutton [package="[THT]"]
  SW1 = PowerSwitch Tail II
  U1 = 2-Channel 5v Relay Shield [package=relay-2ch5v10a]
  U2 = 2-Channel 5v Relay Shield [package=relay-2ch5v10a]

nets:
  N1: IC1.GPB0, S5.Pin_3, S5.Pin_4
  N2: IC1.GPB2, R1.Pin_0
  N3: IC1.GPB3, R2.Pin_0
  N4: IC1.GPB4, R3.Pin_0
  N5: IC1.GPB5, R4.Pin_0
  N6: IC1.GPB6, R5.Pin_0
  VCC: IC1.VDD, U1.VCC, U2.VCC
  GND: IC1.VSS, IC1.GPA0, IC1.GPA1, LED1.cathode, LED2.cathode, LED3.cathode, LED4.cathode, LED5.cathode, U1.GND, U1.IN1, U1.IN2, U2.GND
  N7: IC1.A0, IC1.A1, IC1.A2, S1.Pin_2, S2.Pin_1, S2.Pin_2, S3.Pin_1, S3.Pin_2, S4.Pin_1, S4.Pin_2, S5.Pin_1, S5.Pin_2, SW1.-in
  N8: IC1.GPA2, U2.IN1
  N9: IC1.GPA3, U2.IN2
  N10: IC1.GPA4, S1.Pin_3, S1.Pin_4
  N11: IC1.GPA5, S2.Pin_3, S2.Pin_4
  N12: IC1.GPA6, S3.Pin_3, S3.Pin_4
  N13: IC1.GPA7, S4.Pin_3, S4.Pin_4
  N14: Appliance_#1.POS, U1.K1-On
  N15: Appliance_#1.NEG, Appliance_#2.NEG, Appliance_#3.NEG, Appliance_#4.NEG, 12V_Power_Supply.NEG
  N16: Appliance_#2.POS, U1.K2-On
  N17: Appliance_#3.POS, U2.K1-On
  N18: Appliance_#4.POS, U2.K2-On
  N19: 12V_Power_Supply.POS, U1.K1-In, U1.K2-In, U2.K1-In, U2.K2-In

custom parts:
  Adafruit Pi Cobbler: Adafruit Pi Cobbler GPIO Breakout for Raspberry Pi
  MCP23017 I2C I/O Expander: The MCP23017 uses two i2c pins (these can be shared with other i2c devices), and in exchange gives you 16 general purpose pins. You can set each of 16 pins to be input, output, input with a pullup or open drain. There's even the ability to get an interrupt via an external pin when any of the inputs change so you don't have to keep polling the chip.
  2-Channel 5v Relay Shield: 2 Channel 5v Relay Shield w. 2x SPD-06VDC-SD-C
